# Fritzing sketch PCB EV (saved by Fritzing 0.9.3b)
circuit board: 6.69408cm x 5.76286cm
breadboards: 1

parts:
  - = Battery block 9V
  Arduino = Arduino Nano (Rev3.0) (ICSP)
  Sensor = Adafruit BME280
  HM-10 = Bluetooth HC-06d [package=THT]

nets:
  GND: -.-, Arduino.GND, Sensor.GND, HM-10.GND
  N1: -.+, Arduino.VIN
  N2: Arduino.D1/TX, HM-10.RXD
  N3: Arduino.D0/RX, HM-10.TXD
  5V: Arduino.5V, Sensor.VIN, HM-10.VCC
  N4: Arduino.A5, Sensor.SCK/SCL
  N5: Arduino.A4, Sensor.SDI/SDA

notes:
  Plataforma EV, Módulo de transmisión de datos de presión, temperatura y humedad relativa mediante Bluetooth, 1

custom parts:
  Adafruit BME280: Bosch has stepped up their game with their new BME280 sensor, an environmental sensor with temperature, barometric pressure and humidity! This sensor is great for all sorts of weather/environmental sensing and can even be used in both I2C and SPI! This precision sensor from Bosch is the best low-cost sensing solution for measuring humidity with ±3% accuracy, barometric pressure with ±1 hPa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
  Bluetooth HC-06d: Bluetooth HC-06 - face down, pins down 16.5mm x 37.5mm PCB
